# Fritzing sketch usb_pow_board (saved by Fritzing 0.7.11b)
breadboards: 1

parts:
  USB_POW_IN = USB connector [package=THT]
  TO_DEVICE = USB connector [package=THT]
  POW_IN = Power plug
  S1 = Toggle Switch [package=THT]

nets:
  N1: USB_POW_IN.5V, S1.L1
  GND: USB_POW_IN.GND, USB_POW_IN.chassis5, USB_POW_IN.chassis6, TO_DEVICE.GND, TO_DEVICE.chassis5, TO_DEVICE.chassis6, POW_IN.GND
  N2: TO_DEVICE.5V, S1.COM
  N3: POW_IN.VCC, S1.L2

notes:
  usb_pow - P.O. r1
